// Logisim project q1.circ as structural Verilog: 11 circuits, main circuit Q1_SR_Latch
module Q1_SR_Latch (
  input  S,
  input  R,
  output Q,
  output nQ
);

  nand nand_1 (Q, ~S, nQ);  // NAND_Gate
  nand nand_2 (nQ, Q, ~R);  // NAND_Gate
endmodule

module D_Latch (
  input  D,
  input  CLK,
  output out_3,
  output out_4
);

  wire and_1_out, and_2_out, not_1_out;

  not not_1 (not_1_out, D);
  and and_1 (and_1_out, D, CLK);
  and and_2 (and_2_out, not_1_out, CLK);
  Q1_SR_Latch q1_sr_latch_1 (.S(and_1_out), .R(and_2_out), .Q(out_3), .nQ(out_4));
endmodule

module D_FF (
  input  D,
  input  CLK,
  output out_3,
  output out_4
);

  wire d_latch_1_out_3, not_1_out;

  not not_1 (not_1_out, CLK);
  D_Latch d_latch_1 (.D(D), .CLK(not_1_out), .out_3(d_latch_1_out_3));  // open: out_4
  D_Latch d_latch_2 (.D(d_latch_1_out_3), .CLK(CLK), .out_3(out_3), .out_4(out_4));
endmodule

module Q2_D_FF_P (
  input  D,
  input  nRST,
  output out_3,
  output out_4
);

  wire CLK_out, or_1_out;

  Clock CLK (.out(CLK_out));
  or or_1 (or_1_out, D, nRST);
  D_FF d_ff_1 (.D(or_1_out), .out_3(out_3), .out_4(out_4), .CLK(CLK_out));
endmodule

module Q3_D_FF_N (
  input  nRST_N,
  input  D,
  input  CLK,
  output out_4,
  output out_5
);

  wire d_ff_1_out_3;

  D_FF d_ff_1 (.D(D), .out_3(d_ff_1_out_3), .out_4(out_5), .CLK(CLK));
  and and_1 (out_4, nRST_N, d_ff_1_out_3);
endmodule

module Q3_4bitCounter (
  input  in_1,
  output [3:0] out_2
);

  wire clock_1_out;
  wire [3:0] adder_1_out;

  Adder #(.width(4)) adder_1 (.a(out_2), .b(4'b0001), .out(adder_1_out), .cin(1'b0));  // open: cout
  Clock clock_1 (.out(clock_1_out));
  _4bitReg u_4bitreg_1 (.in_1(adder_1_out), .CLK(clock_1_out), .nRST(in_1), .out_4(out_2));
endmodule

module _4bitReg (
  input  [3:0] in_1,
  input  CLK,
  input  nRST,
  output [3:0] out_4
);

  wire and_1_out, and_2_out, and_3_out, and_4_out;

  and and_1 (and_1_out, nRST, in_1[3]);
  and and_2 (and_2_out, nRST, in_1[2]);
  and and_3 (and_3_out, nRST, in_1[1]);
  and and_4 (and_4_out, nRST, in_1[0]);
  Q3_D_FF_N q3_d_ff_n_1 (.nRST_N(1'b1), .D(and_1_out), .CLK(CLK), .out_4(out_4[3]));  // open: out_5
  Q3_D_FF_N q3_d_ff_n_2 (.nRST_N(1'b1), .D(and_2_out), .CLK(CLK), .out_4(out_4[2]));  // open: out_5
  Q3_D_FF_N q3_d_ff_n_3 (.nRST_N(1'b1), .D(and_3_out), .CLK(CLK), .out_4(out_4[1]));  // open: out_5
  Q3_D_FF_N q3_d_ff_n_4 (.nRST_N(1'b1), .D(and_4_out), .CLK(CLK), .out_4(out_4[0]));  // open: out_5
endmodule

module Q4Sel (
  input  [3:0] in_1,
  output [3:0] out_2
);

  wire and_1_out, and_2_out, not_1_out, not_2_out, not_3_out, not_4_out, not_5_out, not_6_out;

  not not_1 (not_1_out, in_1[2]);
  not not_2 (not_2_out, in_1[1]);
  not not_3 (not_3_out, in_1[0]);
  not not_4 (not_4_out, in_1[3]);
  not not_5 (not_5_out, in_1[2]);
  not not_6 (not_6_out, in_1[0]);
  and and_1 (and_1_out, not_1_out, not_2_out, not_3_out);
  and and_2 (and_2_out, not_4_out, not_5_out, not_6_out);
  or or_1 (out_2[3], and_1_out, in_1[3]);
  or or_2 (out_2[1], and_2_out, in_1[1]);

  assign {out_2[2], out_2[0]} = {in_1[2], in_1[0]};
endmodule

module Q4_0to9 (
  input  in_1,
  output [3:0] out_2
);

  wire clock_1_out;
  wire [3:0] n4bitreg_1_out_4, subtractor_1_out;

  Subtractor #(.width(4)) subtractor_1 (.a(out_2), .b(4'b0001), .out(subtractor_1_out), .bin(1'b0));  // open: bout
  Q4Sel_2 q4sel_2_1 (.in_1(n4bitreg_1_out_4), .out_2(out_2));
  Clock clock_1 (.out(clock_1_out));
  _4bitReg u_4bitreg_1 (.in_1(subtractor_1_out), .CLK(clock_1_out), .nRST(in_1), .out_4(n4bitreg_1_out_4));
endmodule

module Q5Sample (
  input  in_1,
  output [3:0] out_2
);

  wire clock_1_out, not_1_out;
  wire [3:0] n4bitreg_1_out_4, subtractor_1_out;

  Subtractor #(.width(4)) subtractor_1 (.a(out_2), .b(4'b0001), .out(subtractor_1_out), .bin(1'b0));  // open: bout
  Clock clock_1 (.out(clock_1_out));
  not not_1 (not_1_out, in_1);
  Q4Sel_2 q4sel_2_1 (.in_1(n4bitreg_1_out_4), .out_2(out_2));
  _4bitReg u_4bitreg_1 (.in_1(subtractor_1_out), .CLK(clock_1_out), .nRST(not_1_out), .out_4(n4bitreg_1_out_4));
endmodule

module Q4Sel_2 (
  input  [3:0] in_1,
  output [3:0] out_2
);

  wire and_1_out, and_2_out, not_1_out, not_2_out, not_3_out, not_4_out, not_5_out, not_6_out;

  not not_1 (not_1_out, in_1[2]);
  and and_1 (and_1_out, not_1_out, not_2_out, not_3_out);
  not not_2 (not_2_out, in_1[1]);
  not not_3 (not_3_out, in_1[0]);
  not not_4 (not_4_out, in_1[3]);
  and and_2 (and_2_out, not_4_out, not_5_out, not_6_out);
  not not_5 (not_5_out, in_1[2]);
  not not_6 (not_6_out, in_1[1]);
  or or_1 (out_2[3], and_1_out, in_1[3]);
  or or_2 (out_2[0], and_2_out, in_1[0]);

  assign out_2[2:1] = in_1[2:1];
endmodule
